# Fritzing sketch remote (saved by Fritzing 0.9.9b)
breadboards: 1

parts:
  Part1 = Arduino Uno (Rev3)
  Part2 = Thumb Joystick
  Part3 = NRF24L01+ Breakout Board
  Display1 = LCD screen 16x2 IIC [part_number=101290]

nets:
  N1: Part1.A0, Part2.VERT
  N2: Part1.A1, Part2.HORZ
  N3: Part1.A4/SDA, Display1.SDA
  N4: Part1.A5/SCL, Display1.SCL
  N5: Part1.D8, Part3.CS
  N6: Part1.D11_PWM/MOSI, Part3.MOSI
  N7: Part1.D12/MISO, Part3.MISO
  N8: Part1.D13/SCK, Part3.SCK
  N9: Part1.D6_PWM, Part2.SEL
  N10: Part1.D7, Part3.CE
  VCC: Part1.5V, Part2.VCC, Part3.VCC, Display1.VCC
  GND: Part1.GND, Part2.GND, Part3.GND, Display1.GND

custom parts:
  LCD screen 16x2 IIC: LCD screen with HD44780 controller enables showing text, symbols, value or anything else that comes from Croduino/Arduino. It is capable of showing 16 symbols in two lines and therefore can be used in many projects that need to send clearly visible and legible output information.. • Color of symbols: White • Backlight: Blue • Dimensions: 80 x 36 x 12 mm • Screen dimensions: 64.5 x 16 mm •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
