# Fritzing sketch robot (saved by Fritzing 0.9.9b)
breadboards: 1

parts:
  Part1 = Arduino Uno (Rev3)
  HC-SR04_Sensor_1 = HC-SR04 Ultrasonic Distance Sensor
  Part2 = NRF24L01+ Breakout Board
  HC-SR04_Sensor_2 = HC-SR04 Ultrasonic Distance Sensor
  M1 = DC Motor
  M2 = DC Motor
  J1 = Piezo Speaker
  S1 = H-Bridge with L298N

nets:
  N1: Part1.A0, S1.IN1
  N2: Part1.A1, S1.IN2
  N3: Part1.A2, S1.IN3
  N4: Part1.A3, S1.IN4
  N5: Part1.D8, Part2.CE
  N6: Part1.D9_PWM, J1.pin2
  N7: Part1.D10_PWM/SS, Part2.CS
  N8: Part1.D11_PWM/MOSI, Part2.MOSI
  N9: Part1.D12/MISO, Part2.MISO
  N10: Part1.D13/SCK, Part2.SCK
  N11: Part1.D2, HC-SR04_Sensor_1.ECHO
  N12: Part1.D3_PWM, HC-SR04_Sensor_1.TRIG
  N13: Part1.D6_PWM, HC-SR04_Sensor_2.TRIG
  N14: Part1.D7, HC-SR04_Sensor_2.ECHO
  VCC: HC-SR04_Sensor_1.VCC, Part2.VCC, HC-SR04_Sensor_2.VCC
  GND: HC-SR04_Sensor_1.GND, Part2.GND, HC-SR04_Sensor_2.GND, J1.pin1, S1.GND
  N15: M1.pin_1, S1.M2-02
  N16: M1.pin_2, S1.M2-01
  N17: M2.pin_1, S1.M1-02
  N18: M2.pin_2, S1.M1-01
  N19: S1.ENA, S1.ENA-5V
  N20: S1.ENB, S1.ENB-5V

custom parts:
  H-Bridge with L298N: h-bridge
