# Fritzing sketch robot2 (saved by Fritzing 0.9.9b)
breadboards: 1

parts:
  M1 = DC Motor
  M2 = DC Motor
  M3 = DC Motor
  M4 = DC Motor  # not connected
  Part1 = Arduino Uno (Rev3)
  S1 = H-Bridge with L298N
  S2 = H-Bridge with L298N
  HC-SR04_Sensor_1 = HC-SR04 Ultrasonic Distance Sensor
  HC-SR04_Sensor_2 = HC-SR04 Ultrasonic Distance Sensor
  Part2 = NRF24L01+ Breakout Board
  J1 = Piezo Speaker
  U1 = PCF8574 [package="DIP16 [THT]"]
  Power_plug1 = Power plug

nets:
  N1: M1.pin_1, M1.pin_2, M2.pin_1, S1.M1-02, S1.M2-01, S1.M2-02
  N2: M2.pin_2, S1.M1-01
  N3: M3.pin_1, S2.M2-02
  N4: M3.pin_2, S2.M2-01
  N5: Part1.A4/SDA, U1.SDA
  N6: Part1.A5/SCL, U1.SCL
  N7: Part1.D8, Part2.CE
  N8: Part1.D9_PWM, J1.pin2
  N9: Part1.D10_PWM/SS, Part2.CS
  N10: Part1.D11_PWM/MOSI, Part2.MOSI
  N11: Part1.D12/MISO, Part2.MISO
  N12: Part1.D13/SCK, Part2.SCK
  N13: Part1.D2, HC-SR04_Sensor_1.ECHO
  N14: Part1.D3_PWM, HC-SR04_Sensor_1.TRIG
  N15: Part1.D6_PWM, HC-SR04_Sensor_2.TRIG
  N16: Part1.D7, HC-SR04_Sensor_2.ECHO
  VCC: Part1.5V, HC-SR04_Sensor_1.VCC, HC-SR04_Sensor_2.VCC, Part2.VCC, U1.A0, U1.A1, U1.VCC
  GND: Part1.GND, HC-SR04_Sensor_1.GND, HC-SR04_Sensor_2.GND, Part2.GND, J1.pin1, U1.A2, U1.GND
  GND_2: S1.GND, S2.GND, Power_plug1.GND
  N17: S1.ENA, S1.ENA-5V
  N18: S1.IN1, U1.P4
  N19: S1.IN2, U1.P5
  N20: S1.IN3, U1.P6
  N21: S1.IN4, U1.P7
  N22: S1.ENB, S1.ENB-5V
  12V: S2.12V, Power_plug1.VCC
  N23: S2.ENA, S2.ENA-5V
  N24: S2.IN1, U1.P0
  N25: S2.IN2, U1.P1
  N26: S2.IN3, U1.P2
  N27: S2.IN4, U1.P3
  N28: S2.ENB, S2.ENB-5V

custom parts:
  H-Bridge with L298N: h-bridge
